// Logisim project demod_basic.circ as structural Verilog: 2 circuits, main circuit main
module main (
  input  X,
  input  Q3,
  input  Q2,
  input  Q1,
  input  Q0,
  output Z
);

  wire and_1_out, clock_1_out, statelogic_1_r;
  wire [3:0] counter_1_q;

  Clock clock_1 (.out(clock_1_out));
  Counter #(.max('hf), .width(4)) counter_1 (
    .clr(and_1_out), .load(1'b0), .up(1'b1), .count(1'b1), .clk(clock_1_out), .Q(counter_1_q));  // open: D, carry
  and and_1 (and_1_out, statelogic_1_r, clock_1_out);
  STATELOGIC statelogic_1 (.Q3(Q3), .Q2(Q2), .Q1(Q1), .Q0(Q0), .X(X), .R(statelogic_1_r), .Z(Z));
endmodule

module STATELOGIC (
  input  Q3,
  input  Q2,
  input  Q1,
  input  Q0,
  input  X,
  output R,
  output Z
);

  wire and_1_out, and_2_out, and_3_out, nand_1_out, nand_2_out, nand_3_out, nand_4_out, nand_5_out,
       nand_6_out, nand_7_out, nand_8_out, nand_9_out, nand_10_out, nand_11_out, nand_12_out, nand_13_out,
       nand_14_out, nand_15_out, nand_16_out, nand_17_out, nand_18_out, not_1_out, not_2_out;

  not not_1 (not_1_out, Q3);
  not not_2 (not_2_out, X);
  nand nand_1 (nand_1_out, 1'b1, Q1);
  nand nand_2 (nand_2_out, 1'b1, X);
  nand nand_3 (nand_3_out, 1'b1, Q1);
  nand nand_4 (nand_4_out, 1'b1, X);
  and and_1 (and_1_out, not_1_out, Q2);
  nand nand_5 (nand_5_out, nand_1_out, nand_2_out);
  nand nand_6 (nand_6_out, Q1, X);
  nand nand_7 (nand_7_out, nand_3_out, nand_4_out);
  nand nand_8 (nand_8_out, Q1, X);
  nand nand_9 (nand_9_out, 1'b1, Q2);
  nand nand_10 (nand_10_out, 1'b1, Q3);
  nand nand_11 (nand_11_out, 1'b1, Q2);
  nand nand_12 (nand_12_out, 1'b1, Q3);
  and and_2 (and_2_out, and_1_out, Q1);
  and and_3 (and_3_out, Q0, not_2_out);
  nand nand_13 (nand_13_out, nand_5_out, nand_6_out);
  nand nand_14 (nand_14_out, nand_7_out, nand_8_out);
  nand nand_15 (nand_15_out, nand_9_out, nand_10_out);
  nand nand_16 (nand_16_out, nand_11_out, nand_12_out);
  and and_4 (Z, and_2_out, and_3_out);
  nand nand_17 (nand_17_out, nand_13_out, nand_14_out);
  nand nand_18 (nand_18_out, nand_15_out, nand_16_out);
  nand nand_19 (R, nand_17_out, nand_18_out);
endmodule
